# Fritzing sketch AdruinoPWM (saved by Fritzing 0.9.3b)
breadboards: 1

parts:
  Bauteil1 = Arduino Micro (Rev3)  # not connected
  M1 = DC Motor
  Q1 = npn-Powertransistor [package="TO220 [THT]"]
  R1 = Resistor [tolerance=±5% resistance=1k package="0402 [SMD]"]
  R2 = Rotary Potentiometer (Small) [maximum_resistance=100kΩ package=THT]
  Power_plug1 = Power plug

nets:
  N1: M1.pin_1, Q1.collector
  N2: M1.pin_2, Q1.emitter, R2.leg2, Power_plug1.GND
  N3: Q1.base, R1.Pin_1

notes:
  12V
  BD 911
