// Logisim project intel4004.circ as structural Verilog: 18 circuits, main circuit System_4004
module Buendel_6 (
  input  b0,
  input  b1,
  input  b2,
  input  b3,
  input  b4,
  input  b5,
  output [5:0] bus
);


  assign bus = {b5, b4, b3, b2, b1, b0};
endmodule

module Buendel_3 (
  input  b0,
  input  b1,
  input  b2,
  output [2:0] bus
);


  assign bus = {b2, b1, b0};
endmodule

module Buendel_2 (
  input  b0,
  input  b1,
  output [1:0] bus
);


  assign bus = {b1, b0};
endmodule

module Buendel_8 (
  input  b0,
  input  b1,
  input  b2,
  input  b3,
  input  b4,
  input  b5,
  input  b6,
  input  b7,
  output [7:0] bus
);


  assign bus = {b7, b6, b5, b4, b3, b2, b1, b0};
endmodule

module Buendel_4 (
  input  b0,
  input  b1,
  input  b2,
  input  b3,
  output [3:0] bus
);


  assign bus = {b3, b2, b1, b0};
endmodule

module Buendel_12 (
  input  b0,
  input  b1,
  input  b2,
  input  b3,
  input  b4,
  input  b5,
  input  b6,
  input  b7,
  input  b8,
  input  b9,
  input  b10,
  input  b11,
  output [11:0] bus
);


  assign bus = {b11, b10, b9, b8, b7, b6, b5, b4, b3, b2, b1, b0};
endmodule

module Dekoder_3zu8 (
  input  [2:0] A,
  input  EN,
  output Y0,
  output Y1,
  output Y2,
  output Y3,
  output Y4,
  output Y5,
  output Y6,
  output Y7
);

  wire A_0_n, A_1_n, A_2_n;

  and and_1 (Y2, EN, A_0_n, A[1], A_2_n);
  and and_2 (Y6, EN, A_0_n, A[1], A[2]);
  not not_1 (A_0_n, A[0]);
  not not_2 (A_1_n, A[1]);
  and and_3 (Y3, EN, A[0], A[1], A_2_n);
  and and_4 (Y7, EN, A[0], A[1], A[2]);
  not not_3 (A_2_n, A[2]);
  and and_5 (Y4, EN, A_0_n, A_1_n, A[2]);
  and and_6 (Y0, EN, A_0_n, A_1_n, A_2_n);
  and and_7 (Y5, EN, A[0], A_1_n, A[2]);
  and and_8 (Y1, EN, A[0], A_1_n, A_2_n);

  // Other names for the same wires on the sheet: A_0 = A[0]; A_1 = A[1]; A_2 = A[2]

  // Notes on the sheet:
  //   Dekoder 3 auf 8: Y[k] = EN und (A == k). Ersetzt den Demultiplexer (im Web-Simulator erst ab 3 Ausgaengen fehlerhaft).
endmodule

module Dekoder_2zu4 (
  input  [1:0] A,
  input  EN,
  output Y0,
  output Y1,
  output Y2,
  output Y3
);

  wire A_0_n, A_1_n;

  and and_1 (Y3, EN, A[0], A[1]);
  not not_1 (A_0_n, A[0]);
  not not_2 (A_1_n, A[1]);
  and and_2 (Y0, EN, A_0_n, A_1_n);
  and and_3 (Y1, EN, A[0], A_1_n);
  and and_4 (Y2, EN, A_0_n, A[1]);

  // Other names for the same wires on the sheet: A_0 = A[0]; A_1 = A[1]

  // Notes on the sheet:
  //   Dekoder 2 auf 4: Y[k] = EN und (A == k). Ersetzt den Demultiplexer (im Web-Simulator erst ab 3 Ausgaengen fehlerhaft).
endmodule

module Taktgeber (
  input  CLK,
  output [2:0] PH,
  output SYNC
);

  wire [2:0] s1;

  Register #(.width(3)) Phase (.D(s1), .Q(PH), .clk(CLK));  // open: en, clr
  Adder #(.width(3)) adder_1 (.a(PH), .b(3'b001), .out(s1));  // open: cin, cout
  and and_1 (SYNC, PH[0], PH[1], PH[2]);

  // Other names for the same wires on the sheet: PH_0 = PH[0]; PH_1 = PH[1]; PH_2 = PH[2]

  // Notes on the sheet:
  //   Taktgeber: 3-Bit-Zaehler, eine Taktflanke pro Subzyklus. 0=A1 1=A2 2=A3 3=M1 4=M2 5=X1 6=X2 7=X3.
  //   SYNC ist in X3 aktiv; die Peripherie setzt damit ihren eigenen Phasenzaehler auf A1.
endmodule

module Steuerwerk (
  input  [2:0] PH,
  input  C2,
  input  [3:0] OPR,
  input  [3:0] OPA,
  output IRH_WE,
  output IRL_WE,
  output O2H_WE,
  output O2L_WE,
  output PC_WE,
  output PC_WEC,
  output PUSH,
  output POP,
  output ACC_WE,
  output CY_WE,
  output RF_WES,
  output RF_WEP,
  output RF_DSEL,
  output PAIR0,
  output CMROM,
  output CMRAM,
  output C2_WE,
  output C2_D,
  output DCL_WE,
  output CONDSEL,
  output [1:0] PCSEL,
  output [2:0] BS,
  output [1:0] CS,
  output [2:0] RS,
  output [2:0] COS,
  output [1:0] BSRC,
  output [2:0] DOSEL
);

  wire [11:0] MADR;

  ROM #(.addrWidth(12), .dataWidth(3)) u_RS (.addr(MADR), .data(RS));  // open: sel
  ROM #(.addrWidth(12), .dataWidth(2)) u_PCSEL (.addr(MADR), .data(PCSEL));  // open: sel
  ROM #(.addrWidth(12), .dataWidth(3)) u_COS (.addr(MADR), .data(COS));  // open: sel
  ROM #(.addrWidth(12), .dataWidth(3)) u_BS (.addr(MADR), .data(BS));  // open: sel
  ROM #(.addrWidth(12), .dataWidth(2)) u_BSRC (.addr(MADR), .data(BSRC));  // open: sel
  Buendel_12 buendel_12_1 (
    .b0(PH[0]), .b1(PH[1]), .b2(PH[2]), .b3(C2), .b4(OPA[0]), .b5(OPA[1]), .b6(OPA[2]), .b7(OPA[3]),
    .b8(OPR[0]), .b9(OPR[1]), .b10(OPR[2]), .b11(OPR[3]), .bus(MADR));
  ROM #(.addrWidth(12), .dataWidth(2)) u_CS (.addr(MADR), .data(CS));  // open: sel
  ROM #(.addrWidth(12), .dataWidth(3)) u_DOSEL (.addr(MADR), .data(DOSEL));  // open: sel
  ROM #(.addrWidth(12), .dataWidth(20)) Steuer_Flags (
    .addr(MADR),
    .data({CONDSEL, DCL_WE, C2_D, C2_WE, CMRAM, CMROM, PAIR0, RF_DSEL, RF_WEP, RF_WES, CY_WE, ACC_WE, POP, PUSH, PC_WEC, PC_WE, O2L_WE, O2H_WE, IRL_WE, IRH_WE}));  // open: sel

  // Other names for the same wires on the sheet: OPA_0 = OPA[0]; OPA_1 = OPA[1]; OPA_2 = OPA[2]; OPA_3 = OPA[3];
  //   OPR_0 = OPR[0]; OPR_1 = OPR[1]; OPR_2 = OPR[2]; OPR_3 = OPR[3]; PH_0 = PH[0]; PH_1 = PH[1]; PH_2 = PH[2];
  //   STEUER[19:0] = {CONDSEL, DCL_WE, C2_D, C2_WE, CMRAM, CMROM, PAIR0, RF_DSEL, RF_WEP, RF_WES, CY_WE, ACC_WE, POP, PUSH, PC_WEC, PC_WE, O2L_WE, O2H_WE, IRL_WE, IRH_WE}

  // Notes on the sheet:
  //   Steuerwerk: Adresse = OPR<<8 | OPA<<4 | C2<<3 | Phase. Ersetzt den Befehlsdekoder (PLA) des Originals.
  //   C2 = zweiter Maschinenzyklus eines Zwei-Wort-Befehls (JCN FIM FIN JUN JMS ISZ).
  //   contents of RS (hex, n*v repeats v):
  //   2567*0 1 15*0 1 15*0 1 15*0 1 15*0 1 15*0 1 15*0 1 15*0 1 15*0 1 15*0 1 15*0 1 15*0 1 15*0 1 15*0 1
  //   15*0 1 15*0 1 15*0 1 15*0 1 15*0 1 15*0 1 15*0 1 15*0 1 15*0 1 15*0 1 15*0 1 15*0 1 15*0 1 15*0 1
  //   15*0 1 15*0 1 15*0 1 15*0 1 15*0 1 15*0 1 15*0 1 15*0 1 15*0 1 15*0 1 15*0 1 15*0 1 15*0 1 15*0 1
  //   15*0 1 15*0 1 15*0 1 15*0 1 15*0 1 15*0 1 15*0 1 15*0 1 15*0 1 15*0 1 15*0 1 15*0 1 15*0 1 15*0 1
  //   15*0 1 15*0 1 15*0 1 15*0 1 15*0 1 15*0 1 15*0 1 15*0 1 158*0 1 15*0 1 31*0 1 15*0 1 15*0 1 15*0 1
  //   16*0 1 63*0 2 15*0 3 15*0 4 15*0 5 31*0 6 47*0 7
  //   contents of PCSEL (hex, n*v repeats v):
  //   271*0 1 15*0 1 15*0 1 15*0 1 15*0 1 15*0 1 15*0 1 15*0 1 15*0 1 15*0 1 15*0 1 15*0 1 15*0 1 15*0 1
  //   15*0 1 15*0 1 279*0 3 31*0 3 31*0 3 31*0 3 31*0 3 31*0 3 31*0 3 31*0 3 23*0 2 15*0 2 15*0 2 15*0 2
  //   15*0 2 15*0 2 15*0 2 15*0 2 15*0 2 15*0 2 15*0 2 15*0 2 15*0 2 15*0 2 15*0 2 15*0 2 15*0 2 15*0 2
  //   15*0 2 15*0 2 15*0 2 15*0 2 15*0 2 15*0 2 15*0 2 15*0 2 15*0 2 15*0 2 15*0 2 15*0 2 15*0 2 15*0 2
  //   271*0 1 15*0 1 15*0 1 15*0 1 15*0 1 15*0 1 15*0 1 15*0 1 15*0 1 15*0 1 15*0 1 15*0 1 15*0 1 15*0 1
  //   15*0 1 15*0 1
  //   contents of COS (hex, n*v repeats v):
  //   3847*0 3 15*0 3 31*0 5 31*0 1 15*0 2 15*0 3 31*0 3 15*0 4 15*0 6
  //   contents of BS (hex, n*v repeats v):
  //   2311*0 1 15*0 1 15*0 1 15*0 1 15*0 1 15*0 1 15*0 1 15*0 1 15*0 1 15*0 1 15*0 1 15*0 1 15*0 1 15*0 1
  //   15*0 1 15*0 1 1166*0 1 160*0 2 95*0 3 47*0 4
  //   contents of BSRC (hex, n*v repeats v):
  //   3079*0 2 15*0 2 15*0 2 15*0 2 15*0 2 15*0 2 15*0 2 15*0 2 15*0 2 15*0 2 15*0 2 15*0 2 15*0 2 15*0 2
  //   15*0 2 15*0 2 15*0 2 15*0 2 15*0 2 15*0 2 15*0 2 15*0 2 15*0 2 15*0 2 15*0 2 15*0 2 15*0 2 15*0 2
  //   15*0 2 15*0 2 15*0 2 15*0 2 142*0 1 15*0 1 15*0 1 15*0 1 15*0 1 15*0 1 15*0 1 15*0 1 16*0 3
  //   contents of CS (hex, n*v repeats v):
  //   2311*0 1 15*0 1 15*0 1 15*0 1 15*0 1 15*0 1 15*0 1 15*0 1 15*0 1 15*0 1 15*0 1 15*0 1 15*0 1 15*0 1
  //   15*0 1 15*0 1 1166*0 1 160*0 3 95*0 2 47*0 2
  //   contents of DOSEL (hex, n*v repeats v):
  //   1 2 3 13*0 1 2 3 13*0 1 2 3 13*0 1 2 3 13*0 1 2 3 13*0 1 2 3 13*0 1 2 3 13*0 1 2 3 13*0 1 2 3 13*0 1
  //   2 3 13*0 1 2 3 13*0 1 2 3 13*0 1 2 3 13*0 1 2 3 13*0 1 2 3 13*0 1 2 3 13*0 1 2 3 5*0 1 2 3 5*0 1 2 3
  //   5*0 1 2 3 5*0 1 2 3 5*0 1 2 3 5*0 1 2 3 5*0 1 2 3 5*0 1 2 3 5*0 1 2 3 5*0 1 2 3 5*0 1 2 3 5*0 1 2 3
  //   5*0 1 2 3 5*0 1 2 3 5*0 1 2 3 5*0 1 2 3 5*0 1 2 3 5*0 1 2 3 5*0 1 2 3 5*0 1 2 3 5*0 1 2 3 5*0 1 2 3
  //   5*0 1 2 3 5*0 1 2 3 5*0 1 2 3 5*0 1 2 3 5*0 1 2 3 5*0 1 2 3 5*0 1 2 3 5*0 1 2 3 5*0 1 2 3 5*0 1 2 3
  //   5*0 1 2 3 5*0 1 2 3 0 0 0 5 6 8*0 1 2 3 5*0 1 2 3 5*0 1 2 3 0 0 0 5 6 8*0 1 2 3 5*0 1 2 3 5*0 1 2 3
  //   0 0 0 5 6 8*0 1 2 3 5*0 1 2 3 5*0 1 2 3 0 0 0 5 6 8*0 1 2 3 5*0 1 2 3 5*0 1 2 3 0 0 0 5 6 8*0 1 2 3
  //   5*0 1 2 3 5*0 1 2 3 0 0 0 5 6 8*0 1 2 3 5*0 1 2 3 5*0 1 2 3 0 0 0 5 6 8*0 1 2 3 5*0 1 2 3 5*0 1 2 3
  //   0 0 0 5 6 8*0 1 2 3 5*0 6 5 3 5*0 1 2 3 13*0 1 2 3 5*0 6 5 3 5*0 1 2 3 13*0 1 2 3 5*0 6 5 3 5*0 1 2
  //   3 13*0 1 2 3 5*0 6 5 3 5*0 1 2 3 13*0 1 2 3 5*0 6 5 3 5*0 1 2 3 13*0 1 2 3 5*0 6 5 3 5*0 1 2 3 13*0
  //   1 2 3 5*0 6 5 3 5*0 1 2 3 13*0 1 2 3 5*0 6 5 3 5*0 1 2 3 13*0 1 2 3 5*0 1 2 3 5*0 1 2 3 5*0 1 2 3
  //   5*0 1 2 3 5*0 1 2 3 5*0 1 2 3 5*0 1 2 3 5*0 1 2 3 5*0 1 2 3 5*0 1 2 3 5*0 1 2 3 5*0 1 2 3 5*0 1 2 3
  //   5*0 1 2 3 5*0 1 2 3 5*0 1 2 3 5*0 1 2 3 5*0 1 2 3 5*0 1 2 3 5*0 1 2 3 5*0 1 2 3 5*0 1 2 3 5*0 1 2 3
  //   5*0 1 2 3 5*0 1 2 3 5*0 1 2 3 5*0 1 2 3 5*0 1 2 3 5*0 1 2 3 5*0 1 2 3 5*0 1 2 3 5*0 1 2 3 5*0 1 2 3
  //   5*0 1 2 3 5*0 1 2 3 5*0 1 2 3 5*0 1 2 3 5*0 1 2 3 5*0 1 2 3 5*0 1 2 3 5*0 1 2 3 5*0 1 2 3 5*0 1 2 3
  //   5*0 1 2 3 5*0 1 2 3 5*0 1 2 3 5*0 1 2 3 5*0 1 2 3 5*0 1 2 3 5*0 1 2 3 5*0 1 2 3 5*0 1 2 3 5*0 1 2 3
  //   5*0 1 2 3 5*0 1 2 3 5*0 1 2 3 5*0 1 2 3 5*0 1 2 3 5*0 1 2 3 5*0 1 2 3 5*0 1 2 3 5*0 1 2 3 5*0 1 2 3
  //   5*0 1 2 3 13*0 1 2 3 13*0 1 2 3 13*0 1 2 3 13*0 1 2 3 13*0 1 2 3 13*0 1 2 3 13*0 1 2 3 13*0 1 2 3
  //   13*0 1 2 3 13*0 1 2 3 13*0 1 2 3 13*0 1 2 3 13*0 1 2 3 13*0 1 2 3 13*0 1 2 3 13*0 1 2 3 5*0 1 2 3
  //   5*0 1 2 3 5*0 1 2 3 5*0 1 2 3 5*0 1 2 3 5*0 1 2 3 5*0 1 2 3 5*0 1 2 3 5*0 1 2 3 5*0 1 2 3 5*0 1 2 3
  //   5*0 1 2 3 5*0 1 2 3 5*0 1 2 3 5*0 1 2 3 5*0 1 2 3 5*0 1 2 3 5*0 1 2 3 5*0 1 2 3 5*0 1 2 3 5*0 1 2 3
  //   5*0 1 2 3 5*0 1 2 3 5*0 1 2 3 5*0 1 2 3 5*0 1 2 3 5*0 1 2 3 5*0 1 2 3 5*0 1 2 3 5*0 1 2 3 5*0 1 2 3
  //   5*0 1 2 3 13*0 1 2 3 13*0 1 2 3 13*0 1 2 3 13*0 1 2 3 13*0 1 2 3 13*0 1 2 3 13*0 1 2 3 13*0 1 2 3
  //   13*0 1 2 3 13*0 1 2 3 13*0 1 2 3 13*0 1 2 3 13*0 1 2 3 13*0 1 2 3 13*0 1 2 3 13*0 1 2 3 13*0 1 2 3
  //   13*0 1 2 3 13*0 1 2 3 13*0 1 2 3 13*0 1 2 3 13*0 1 2 3 13*0 1 2 3 13*0 1 2 3 13*0 1 2 3 13*0 1 2 3
  //   13*0 1 2 3 13*0 1 2 3 13*0 1 2 3 13*0 1 2 3 13*0 1 2 3 13*0 1 2 3 13*0 1 2 3 13*0 1 2 3 13*0 1 2 3
  //   13*0 1 2 3 13*0 1 2 3 13*0 1 2 3 13*0 1 2 3 13*0 1 2 3 13*0 1 2 3 13*0 1 2 3 13*0 1 2 3 13*0 1 2 3
  //   13*0 1 2 3 13*0 1 2 3 13*0 1 2 3 13*0 1 2 3 13*0 1 2 3 13*0 1 2 3 13*0 1 2 3 13*0 1 2 3 13*0 1 2 3
  //   13*0 1 2 3 13*0 1 2 3 13*0 1 2 3 13*0 1 2 3 13*0 1 2 3 13*0 1 2 3 13*0 1 2 3 13*0 1 2 3 13*0 1 2 3
  //   13*0 1 2 3 13*0 1 2 3 13*0 1 2 3 13*0 1 2 3 13*0 1 2 3 13*0 1 2 3 13*0 1 2 3 13*0 1 2 3 13*0 1 2 3
  //   13*0 1 2 3 13*0 1 2 3 13*0 1 2 3 13*0 1 2 3 13*0 1 2 3 13*0 1 2 3 13*0 1 2 3 13*0 1 2 3 13*0 1 2 3
  //   13*0 1 2 3 13*0 1 2 3 13*0 1 2 3 13*0 1 2 3 13*0 1 2 3 13*0 1 2 3 13*0 1 2 3 13*0 1 2 3 13*0 1 2 3
  //   13*0 1 2 3 13*0 1 2 3 13*0 1 2 3 13*0 1 2 3 13*0 1 2 3 13*0 1 2 3 13*0 1 2 3 0 0 0 4 9*0 1 2 3 0 0 0
  //   4 9*0 1 2 3 0 0 0 4 9*0 1 2 3 0 0 0 4 9*0 1 2 3 0 0 0 4 9*0 1 2 3 0 0 0 4 9*0 1 2 3 0 0 0 4 9*0 1 2
  //   3 0 0 0 4 9*0 1 2 3 13*0 1 2 3 13*0 1 2 3 13*0 1 2 3 13*0 1 2 3 13*0 1 2 3 13*0 1 2 3 13*0 1 2 3
  //   13*0 1 2 3 13*0 1 2 3 13*0 1 2 3 13*0 1 2 3 13*0 1 2 3 13*0 1 2 3 13*0 1 2 3 13*0 1 2 3 13*0 1 2 3
  //   13*0 1 2 3 13*0 1 2 3 13*0 1 2 3 13*0 1 2 3 13*0 1 2 3 13*0 1 2 3 13*0 1 2 3
  //   contents of Steuer_Flags (hex, n*v repeats v):
  //   0 0 0 1 12 0 0 10000 11*0 1 12 0 0 10000 11*0 1 12 0 0 10000 11*0 1 12 0 0 10000 11*0 1 12 0 0 10000
  //   11*0 1 12 0 0 10000 11*0 1 12 0 0 10000 11*0 1 12 0 0 10000 11*0 1 12 0 0 10000 11*0 1 12 0 0 10000
  //   11*0 1 12 0 0 10000 11*0 1 12 0 0 10000 11*0 1 12 0 0 10000 11*0 1 12 0 0 10000 11*0 1 12 0 0 10000
  //   11*0 1 12 0 0 10000 11*0 1 12 0 0 30000 0 0 0 4 18 0 0 10020 0 0 0 1 12 0 0 30000 0 0 0 4 18 0 0
  //   10020 0 0 0 1 12 0 0 30000 0 0 0 4 18 0 0 10020 0 0 0 1 12 0 0 30000 0 0 0 4 18 0 0 10020 0 0 0 1 12
  //   0 0 30000 0 0 0 4 18 0 0 10020 0 0 0 1 12 0 0 30000 0 0 0 4 18 0 0 10020 0 0 0 1 12 0 0 30000 0 0 0
  //   4 18 0 0 10020 0 0 0 1 12 0 0 30000 0 0 0 4 18 0 0 10020 0 0 0 1 12 0 0 30000 0 0 0 4 18 0 0 10020 0
  //   0 0 1 12 0 0 30000 0 0 0 4 18 0 0 10020 0 0 0 1 12 0 0 30000 0 0 0 4 18 0 0 10020 0 0 0 1 12 0 0
  //   30000 0 0 0 4 18 0 0 10020 0 0 0 1 12 0 0 30000 0 0 0 4 18 0 0 10020 0 0 0 1 12 0 0 30000 0 0 0 4 18
  //   0 0 10020 0 0 0 1 12 0 0 30000 0 0 0 4 18 0 0 10020 0 0 0 1 12 0 0 30000 0 0 0 4 18 0 0 10020 0 0 0
  //   1 12 0 0 30000 0 0 0 4 18 0 0 10800 0 0 0 1 12 0 c000 10000 11*0 1 12 0 0 30000 0 0 0 4 18 0 0 10800
  //   0 0 0 1 12 0 c000 10000 11*0 1 12 0 0 30000 0 0 0 4 18 0 0 10800 0 0 0 1 12 0 c000 10000 11*0 1 12 0
  //   0 30000 0 0 0 4 18 0 0 10800 0 0 0 1 12 0 c000 10000 11*0 1 12 0 0 30000 0 0 0 4 18 0 0 10800 0 0 0
  //   1 12 0 c000 10000 11*0 1 12 0 0 30000 0 0 0 4 18 0 0 10800 0 0 0 1 12 0 c000 10000 11*0 1 12 0 0
  //   30000 0 0 0 4 18 0 0 10800 0 0 0 1 12 0 c000 10000 11*0 1 12 0 0 30000 0 0 0 4 18 0 0 10800 0 0 0 1
  //   12 0 c000 10000 11*0 1 12 0 0 30000 2000 2000 0 4 8 0 0 10800 0 0 0 1 12 0 0 10010 11*0 1 12 0 0
  //   30000 2000 2000 0 4 8 0 0 10800 0 0 0 1 12 0 0 10010 11*0 1 12 0 0 30000 2000 2000 0 4 8 0 0 10800 0
  //   0 0 1 12 0 0 10010 11*0 1 12 0 0 30000 2000 2000 0 4 8 0 0 10800 0 0 0 1 12 0 0 10010 11*0 1 12 0 0
  //   30000 2000 2000 0 4 8 0 0 10800 0 0 0 1 12 0 0 10010 11*0 1 12 0 0 30000 2000 2000 0 4 8 0 0 10800 0
  //   0 0 1 12 0 0 10010 11*0 1 12 0 0 30000 2000 2000 0 4 8 0 0 10800 0 0 0 1 12 0 0 10010 11*0 1 12 0 0
  //   30000 2000 2000 0 4 8 0 0 10800 0 0 0 1 12 0 0 10010 11*0 1 12 0 0 30000 0 0 0 4 18 0 0 10010 0 0 0
  //   1 12 0 0 30000 0 0 0 4 18 0 0 10010 0 0 0 1 12 0 0 30000 0 0 0 4 18 0 0 10010 0 0 0 1 12 0 0 30000 0
  //   0 0 4 18 0 0 10010 0 0 0 1 12 0 0 30000 0 0 0 4 18 0 0 10010 0 0 0 1 12 0 0 30000 0 0 0 4 18 0 0
  //   10010 0 0 0 1 12 0 0 30000 0 0 0 4 18 0 0 10010 0 0 0 1 12 0 0 30000 0 0 0 4 18 0 0 10010 0 0 0 1 12
  //   0 0 30000 0 0 0 4 18 0 0 10010 0 0 0 1 12 0 0 30000 0 0 0 4 18 0 0 10010 0 0 0 1 12 0 0 30000 0 0 0
  //   4 18 0 0 10010 0 0 0 1 12 0 0 30000 0 0 0 4 18 0 0 10010 0 0 0 1 12 0 0 30000 0 0 0 4 18 0 0 10010 0
  //   0 0 1 12 0 0 30000 0 0 0 4 18 0 0 10010 0 0 0 1 12 0 0 30000 0 0 0 4 18 0 0 10010 0 0 0 1 12 0 0
  //   30000 0 0 0 4 18 0 0 10010 0 0 0 1 12 0 0 30000 0 0 0 4 18 0 0 10050 0 0 0 1 12 0 0 30000 0 0 0 4 18
  //   0 0 10050 0 0 0 1 12 0 0 30000 0 0 0 4 18 0 0 10050 0 0 0 1 12 0 0 30000 0 0 0 4 18 0 0 10050 0 0 0
  //   1 12 0 0 30000 0 0 0 4 18 0 0 10050 0 0 0 1 12 0 0 30000 0 0 0 4 18 0 0 10050 0 0 0 1 12 0 0 30000 0
  //   0 0 4 18 0 0 10050 0 0 0 1 12 0 0 30000 0 0 0 4 18 0 0 10050 0 0 0 1 12 0 0 30000 0 0 0 4 18 0 0
  //   10050 0 0 0 1 12 0 0 30000 0 0 0 4 18 0 0 10050 0 0 0 1 12 0 0 30000 0 0 0 4 18 0 0 10050 0 0 0 1 12
  //   0 0 30000 0 0 0 4 18 0 0 10050 0 0 0 1 12 0 0 30000 0 0 0 4 18 0 0 10050 0 0 0 1 12 0 0 30000 0 0 0
  //   4 18 0 0 10050 0 0 0 1 12 0 0 30000 0 0 0 4 18 0 0 10050 0 0 0 1 12 0 0 30000 0 0 0 4 18 0 0 10050 0
  //   0 0 1 12 0 0 11400 11*0 1 12 0 0 11400 11*0 1 12 0 0 11400 11*0 1 12 0 0 11400 11*0 1 12 0 0 11400
  //   11*0 1 12 0 0 11400 11*0 1 12 0 0 11400 11*0 1 12 0 0 11400 11*0 1 12 0 0 11400 11*0 1 12 0 0 11400
  //   11*0 1 12 0 0 11400 11*0 1 12 0 0 11400 11*0 1 12 0 0 11400 11*0 1 12 0 0 11400 11*0 1 12 0 0 11400
  //   11*0 1 12 0 0 11400 11*0 1 12 0 0 30000 0 0 0 4 18 0 0 91420 0 0 0 1 12 0 0 30000 0 0 0 4 18 0 0
  //   91420 0 0 0 1 12 0 0 30000 0 0 0 4 18 0 0 91420 0 0 0 1 12 0 0 30000 0 0 0 4 18 0 0 91420 0 0 0 1 12
  //   0 0 30000 0 0 0 4 18 0 0 91420 0 0 0 1 12 0 0 30000 0 0 0 4 18 0 0 91420 0 0 0 1 12 0 0 30000 0 0 0
  //   4 18 0 0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
endmodule

module ALU (
  input  [3:0] A,
  input  CY,
  input  [3:0] B,
  input  [2:0] BS,
  input  [1:0] CS,
  input  [2:0] RS,
  input  [2:0] COS,
  output [3:0] RES,
  output COUT
);

  wire CIN, g2, g3, GT9, KORR, nCY, UEB;
  wire [3:0] BADD, DAA6, KBPv, nA, nB, RALv, RARv, SUMME, TCCv, TCSv;

  assign nA = ~A;  // NOT_Gate not_1, 4 bits wide
  Buendel_4 buendel_4_1 (.b0(1'b0), .b1(KORR), .b2(KORR), .b3(1'b0), .bus(DAA6));
  Buendel_4 buendel_4_2 (.b0(CY), .b1(A[0]), .b2(A[1]), .b3(A[2]), .bus(RALv));
  assign nB = ~B;  // NOT_Gate not_2, 4 bits wide
  Multiplexer #(.select(3), .enable("false"), .width(4)) multiplexer_1 (
    .in0(SUMME), .in1(B), .in2(nA), .in3(RALv), .in4(RARv), .in5(TCCv), .in6(TCSv), .in7(KBPv), .out(RES),
    .sel(RS));
  Buendel_4 buendel_4_3 (.b0(A[1]), .b1(A[2]), .b2(A[3]), .b3(CY), .bus(RARv));
  not not_3 (nCY, CY);
  or or_1 (g3, CY, UEB);
  or or_2 (g2, A[2], A[1]);
  Buendel_4 buendel_4_4 (.b0(CY), .b1(1'b0), .b2(1'b0), .b3(1'b0), .bus(TCCv));
  Multiplexer #(.select(3), .enable("false"), .width(4)) multiplexer_2 (
    .in0(B), .in1(nB), .in2(4'b0000), .in3(4'b1111), .in4(DAA6), .in5(4'b0000), .in6(4'b0000), .in7(4'b0000),
    .out(BADD), .sel(BS));
  Multiplexer #(.select(3), .enable("false")) multiplexer_3 (
    .in0(UEB), .in1(A[3]), .in2(A[0]), .in3(1'b0), .in4(1'b1), .in5(nCY), .in6(g3), .in7(CY), .out(COUT),
    .sel(COS));
  and and_1 (GT9, A[3], g2);
  Buendel_4 buendel_4_5 (.b0(nCY), .b1(CY), .b2(1'b0), .b3(1'b1), .bus(TCSv));
  or or_3 (KORR, GT9, CY);
  Multiplexer #(.select(2), .enable("false")) multiplexer_4 (
    .in0(CY), .in1(nCY), .in2(1'b0), .in3(1'b1), .out(CIN), .sel(CS));
  Adder #(.width(4)) adder_1 (.a(A), .b(BADD), .out(SUMME), .cin(CIN), .cout(UEB));
  ROM #(.addrWidth(4), .dataWidth(4)) KBP_Tabelle (.addr(A), .data(KBPv));  // open: sel

  // Other names for the same wires on the sheet: A_0 = A[0]; A_1 = A[1]; A_2 = A[2]; A_3 = A[3]

  // Notes on the sheet:
  //   ALU: ein 4-Bit-Addierer mit waehlbarem Operanden (BS) und Uebertrag (CS), Ergebnis-Mux (RS), Carry-Mux (COS).
  //   SUB/SBM = A + ~B + ~CY, DAC = A + F, IAC = A + 0 + 1, DAA addiert 6 wenn A>9 oder CY.
  //   contents of KBP_Tabelle (hex, n*v repeats v):
  //   0 1 2 f 3 f f f 4 7*f
endmodule

module Indexregister (
  input  CLK,
  input  [2:0] PADR,
  input  UNGERADE,
  input  [3:0] WD,
  input  [3:0] DH,
  input  [3:0] DL,
  input  WE1,
  input  WE2,
  output [3:0] REVEN,
  output [3:0] RODD,
  output [3:0] RSEL,
  output [7:0] P0,
  output [7:0] P1,
  output [7:0] P2,
  output [7:0] P3,
  output [7:0] P4,
  output [7:0] P5,
  output [7:0] P6,
  output [7:0] P7
);

  wire EN_G, EN_U, g4, g5, nODD, WG0, WG1, WG2, WG3, WG4, WG5, WG6, WG7, WU0, WU1, WU2, WU3, WU4, WU5, WU6,
       WU7;
  wire [3:0] D_G, D_U, R0, R1, R2, R3, R4, R5, R6, R7, R8, R9, R10, R11, R12, R13, R14, R15;

  Multiplexer #(.select(1), .enable("false"), .width(4)) multiplexer_1 (.in0(WD), .in1(DH), .out(D_G), .sel(WE2));
  Register #(.width(4)) u_R0 (.D(D_G), .en(WG0), .Q(R0), .clk(CLK));  // open: clr
  Register #(.width(4)) u_R5 (.D(D_U), .en(WU2), .Q(R5), .clk(CLK));  // open: clr
  Register #(.width(4)) u_R10 (.D(D_G), .en(WG5), .Q(R10), .clk(CLK));  // open: clr
  Register #(.width(4)) u_R15 (.D(D_U), .en(WU7), .Q(R15), .clk(CLK));  // open: clr
  Multiplexer #(.select(3), .enable("false"), .width(4)) multiplexer_2 (
    .in0(R1), .in1(R3), .in2(R5), .in3(R7), .in4(R9), .in5(R11), .in6(R13), .in7(R15), .out(RODD), .sel(PADR));
  Buendel_8 buendel_8_1 (
    .b0(R5[0]), .b1(R5[1]), .b2(R5[2]), .b3(R5[3]), .b4(R4[0]), .b5(R4[1]), .b6(R4[2]), .b7(R4[3]), .bus(P2));
  Buendel_8 buendel_8_2 (
    .b0(R15[0]), .b1(R15[1]), .b2(R15[2]), .b3(R15[3]), .b4(R14[0]), .b5(R14[1]), .b6(R14[2]), .b7(R14[3]),
    .bus(P7));
  Multiplexer #(.select(1), .enable("false"), .width(4)) multiplexer_3 (.in0(WD), .in1(DL), .out(D_U), .sel(WE2));
  Register #(.width(4)) u_R1 (.D(D_U), .en(WU0), .Q(R1), .clk(CLK));  // open: clr
  Register #(.width(4)) u_R6 (.D(D_G), .en(WG3), .Q(R6), .clk(CLK));  // open: clr
  Register #(.width(4)) u_R11 (.D(D_U), .en(WU5), .Q(R11), .clk(CLK));  // open: clr
  not not_1 (nODD, UNGERADE);
  Multiplexer #(.select(1), .enable("false"), .width(4)) multiplexer_4 (
    .in0(REVEN), .in1(RODD), .out(RSEL), .sel(UNGERADE));
  Buendel_8 buendel_8_3 (
    .b0(R9[0]), .b1(R9[1]), .b2(R9[2]), .b3(R9[3]), .b4(R8[0]), .b5(R8[1]), .b6(R8[2]), .b7(R8[3]), .bus(P4));
  Dekoder_3zu8 dekoder_3zu8_1 (
    .A(PADR), .EN(EN_G), .Y0(WG0), .Y1(WG1), .Y2(WG2), .Y3(WG3), .Y4(WG4), .Y5(WG5), .Y6(WG6), .Y7(WG7));
  and and_1 (g4, WE1, nODD);
  Register #(.width(4)) u_R2 (.D(D_G), .en(WG1), .Q(R2), .clk(CLK));  // open: clr
  Register #(.width(4)) u_R7 (.D(D_U), .en(WU3), .Q(R7), .clk(CLK));  // open: clr
  Buendel_8 buendel_8_4 (
    .b0(R3[0]), .b1(R3[1]), .b2(R3[2]), .b3(R3[3]), .b4(R2[0]), .b5(R2[1]), .b6(R2[2]), .b7(R2[3]), .bus(P1));
  Register #(.width(4)) u_R12 (.D(D_G), .en(WG6), .Q(R12), .clk(CLK));  // open: clr
  Buendel_8 buendel_8_5 (
    .b0(R13[0]), .b1(R13[1]), .b2(R13[2]), .b3(R13[3]), .b4(R12[0]), .b5(R12[1]), .b6(R12[2]), .b7(R12[3]),
    .bus(P6));
  or or_1 (EN_G, WE2, g4);
  Register #(.width(4)) u_R3 (.D(D_U), .en(WU1), .Q(R3), .clk(CLK));  // open: clr
  Register #(.width(4)) u_R8 (.D(D_G), .en(WG4), .Q(R8), .clk(CLK));  // open: clr
  Dekoder_3zu8 dekoder_3zu8_2 (
    .A(PADR), .EN(EN_U), .Y0(WU0), .Y1(WU1), .Y2(WU2), .Y3(WU3), .Y4(WU4), .Y5(WU5), .Y6(WU6), .Y7(WU7));
  Register #(.width(4)) u_R13 (.D(D_U), .en(WU6), .Q(R13), .clk(CLK));  // open: clr
  Buendel_8 buendel_8_6 (
    .b0(R7[0]), .b1(R7[1]), .b2(R7[2]), .b3(R7[3]), .b4(R6[0]), .b5(R6[1]), .b6(R6[2]), .b7(R6[3]), .bus(P3));
  and and_2 (g5, WE1, UNGERADE);
  Buendel_8 buendel_8_7 (
    .b0(R1[0]), .b1(R1[1]), .b2(R1[2]), .b3(R1[3]), .b4(R0[0]), .b5(R0[1]), .b6(R0[2]), .b7(R0[3]), .bus(P0));
  Register #(.width(4)) u_R4 (.D(D_G), .en(WG2), .Q(R4), .clk(CLK));  // open: clr
  Register #(.width(4)) u_R9 (.D(D_U), .en(WU4), .Q(R9), .clk(CLK));  // open: clr
  Register #(.width(4)) u_R14 (.D(D_G), .en(WG7), .Q(R14), .clk(CLK));  // open: clr
  Multiplexer #(.select(3), .enable("false"), .width(4)) multiplexer_5 (
    .in0(R0), .in1(R2), .in2(R4), .in3(R6), .in4(R8), .in5(R10), .in6(R12), .in7(R14), .out(REVEN), .sel(PADR));
  Buendel_8 buendel_8_8 (
    .b0(R11[0]), .b1(R11[1]), .b2(R11[2]), .b3(R11[3]), .b4(R10[0]), .b5(R10[1]), .b6(R10[2]), .b7(R10[3]),
    .bus(P5));
  or or_2 (EN_U, WE2, g5);

  // Other names for the same wires on the sheet: R0_0 = R0[0]; R0_1 = R0[1]; R0_2 = R0[2]; R0_3 = R0[3]; R1_0 = R1[0];
  //   R1_1 = R1[1]; R1_2 = R1[2]; R1_3 = R1[3]; R2_0 = R2[0]; R2_1 = R2[1]; R2_2 = R2[2]; R2_3 = R2[3]; R3_0 = R3[0];
  //   R3_1 = R3[1]; R3_2 = R3[2]; R3_3 = R3[3]; R4_0 = R4[0]; R4_1 = R4[1]; R4_2 = R4[2]; R4_3 = R4[3]; R5_0 = R5[0];
  //   R5_1 = R5[1]; R5_2 = R5[2]; R5_3 = R5[3]; R6_0 = R6[0]; R6_1 = R6[1]; R6_2 = R6[2]; R6_3 = R6[3]; R7_0 = R7[0];
  //   R7_1 = R7[1]; R7_2 = R7[2]; R7_3 = R7[3]; R8_0 = R8[0]; R8_1 = R8[1]; R8_2 = R8[2]; R8_3 = R8[3]; R9_0 = R9[0];
  //   R9_1 = R9[1]; R9_2 = R9[2]; R9_3 = R9[3]; R10_0 = R10[0]; R10_1 = R10[1]; R10_2 = R10[2]; R10_3 = R10[3];
  //   R11_0 = R11[0]; R11_1 = R11[1]; R11_2 = R11[2]; R11_3 = R11[3]; R12_0 = R12[0]; R12_1 = R12[1]; R12_2 = R12[2];
  //   R12_3 = R12[3]; R13_0 = R13[0]; R13_1 = R13[1]; R13_2 = R13[2]; R13_3 = R13[3]; R14_0 = R14[0]; R14_1 = R14[1];
  //   R14_2 = R14[2]; R14_3 = R14[3]; R15_0 = R15[0]; R15_1 = R15[1]; R15_2 = R15[2]; R15_3 = R15[3]

  // Notes on the sheet:
  //   16 Indexregister R0..R15 zu je 4 Bit, als 8 Paare organisiert (gerade = oberes Nibble).
  //   WE1 schreibt ein einzelnes Register (WD), WE2 ein ganzes Paar (DH/DL) - fuer FIM und FIN.
endmodule

module Adressstapel (
  input  CLK,
  input  PUSH,
  input  POP,
  input  WE,
  input  [1:0] PCSEL,
  input  [3:0] O2H,
  input  [3:0] O2L,
  input  [3:0] OPA,
  input  [3:0] REVEN,
  input  [3:0] RODD,
  output [3:0] PCL,
  output [3:0] PCM,
  output [3:0] PCH,
  output [1:0] SP
);

  wire C1, C2, S0EN, S1EN, S2EN, S3EN, SPEN;
  wire [1:0] SPDELTA, SPNEU, WSLOT;
  wire [3:0] INCH, INCL, INCM, NH, NL, NM, S0H, S0L, S0M, S1H, S1L, S1M, S2H, S2L, S2M, S3H, S3L, S3M;

  or or_1 (SPEN, PUSH, POP);
  Register #(.width(2)) u_SP (.D(SPNEU), .en(SPEN), .Q(SP), .clk(CLK));  // open: clr
  Register #(.width(4)) u_S1M (.D(NM), .en(S1EN), .Q(S1M), .clk(CLK));  // open: clr
  Register #(.width(4)) u_S3L (.D(NL), .en(S3EN), .Q(S3L), .clk(CLK));  // open: clr
  Multiplexer #(.select(2), .enable("false"), .width(4)) multiplexer_1 (
    .in0(S0H), .in1(S1H), .in2(S2H), .in3(S3H), .out(PCH), .sel(SP));
  Multiplexer #(.select(2), .enable("false"), .width(4)) multiplexer_2 (
    .in0(INCM), .in1(O2H), .in2(O2H), .in3(REVEN), .out(NM), .sel(PCSEL));
  Multiplexer #(.select(1), .enable("false"), .width(2)) multiplexer_3 (.in0(SP), .in1(SPNEU), .out(WSLOT), .sel(PUSH));
  Register #(.width(4)) u_S0L (.D(NL), .en(S0EN), .Q(S0L), .clk(CLK));  // open: clr
  Register #(.width(4)) u_S1H (.D(NH), .en(S1EN), .Q(S1H), .clk(CLK));  // open: clr
  Register #(.width(4)) u_S3M (.D(NM), .en(S3EN), .Q(S3M), .clk(CLK));  // open: clr
  Adder #(.width(4)) adder_1 (.a(PCL), .b(4'b0000), .out(INCL), .cin(1'b1), .cout(C1));
  Multiplexer #(.select(2), .enable("false"), .width(4)) multiplexer_4 (
    .in0(INCH), .in1(PCH), .in2(OPA), .in3(PCH), .out(NH), .sel(PCSEL));
  Dekoder_2zu4 dekoder_2zu4_1 (.A(WSLOT), .EN(WE), .Y0(S0EN), .Y1(S1EN), .Y2(S2EN), .Y3(S3EN));
  Adder #(.width(4)) adder_2 (.a(PCM), .b(4'b0000), .out(INCM), .cin(C1), .cout(C2));
  Register #(.width(4)) u_S0M (.D(NM), .en(S0EN), .Q(S0M), .clk(CLK));  // open: clr
  Register #(.width(4)) u_S2L (.D(NL), .en(S2EN), .Q(S2L), .clk(CLK));  // open: clr
  Register #(.width(4)) u_S3H (.D(NH), .en(S3EN), .Q(S3H), .clk(CLK));  // open: clr
  Adder #(.width(4)) adder_3 (.a(PCH), .b(4'b0000), .out(INCH), .cin(C2));  // open: cout
  Register #(.width(4)) u_S0H (.D(NH), .en(S0EN), .Q(S0H), .clk(CLK));  // open: clr
  Register #(.width(4)) u_S2M (.D(NM), .en(S2EN), .Q(S2M), .clk(CLK));  // open: clr
  Multiplexer #(.select(2), .enable("false"), .width(4)) multiplexer_5 (
    .in0(S0L), .in1(S1L), .in2(S2L), .in3(S3L), .out(PCL), .sel(SP));
  Buendel_2 buendel_2_1 (.b0(1'b1), .b1(POP), .bus(SPDELTA));
  Register #(.width(4)) u_S1L (.D(NL), .en(S1EN), .Q(S1L), .clk(CLK));  // open: clr
  Register #(.width(4)) u_S2H (.D(NH), .en(S2EN), .Q(S2H), .clk(CLK));  // open: clr
  Multiplexer #(.select(2), .enable("false"), .width(4)) multiplexer_6 (
    .in0(S0M), .in1(S1M), .in2(S2M), .in3(S3M), .out(PCM), .sel(SP));
  Multiplexer #(.select(2), .enable("false"), .width(4)) multiplexer_7 (
    .in0(INCL), .in1(O2L), .in2(O2L), .in3(RODD), .out(NL), .sel(PCSEL));
  Adder #(.width(2)) adder_4 (.a(SP), .b(SPDELTA), .out(SPNEU));  // open: cin, cout

  // Notes on the sheet:
  //   Adressstapel wie im 4004: vier 12-Bit-Adressregister, SP zeigt auf das aktuelle (= Programmzaehler).
  //   JMS: SP+1 und Ziel dort ablegen, BBL: SP-1. Damit drei Unterprogrammebenen; Ueberlauf rotiert wie im Original.
  //   PCSEL: 0 = PC+1, 1 = Seite+O2 (JCN/ISZ), 2 = OPA+O2 (JUN/JMS), 3 = Seite+Registerpaar (JIN).
endmodule

module CPU_4004 (
  input  CLK,
  input  [3:0] D_EIN,
  input  TEST,
  output [3:0] D_AUS,
  output SYNC,
  output CM_ROM,
  output CM_RAM0,
  output CM_RAM1,
  output CM_RAM2,
  output CM_RAM3,
  output [3:0] AKKU,
  output CARRY,
  output [11:0] PC,
  output [7:0] IR,
  output [2:0] PHASE,
  output [1:0] SP,
  output [7:0] R0R1,
  output [7:0] R2R3,
  output [7:0] R4R5,
  output [7:0] R6R7,
  output [7:0] R8R9,
  output [7:0] R10R11,
  output [7:0] R12R13,
  output [7:0] R14R15
);

  wire ACC_0_n, ACC_1_n, ACC_2_n, ACC_3_n, ACC_WE, AKKU0, BED, C2, C2_D, C2_WE, CMRAM, CMROM, CONDSEL, COUT,
       CY_WE, DCL_0_n, DCL_1_n, DCL_2_n, DCL_WE, g6, g7, g8, g9, g10, g11, IRH_WE, IRL_WE, ISZ_OK, JC,
       JCN_OK, nTEST, O2H_WE, O2L_WE, PAIR0, PC_WE, PC_WEC, PCWE, POP, PUSH, RF_DSEL, RF_WEP, RF_WES,
       RINC_0_n, RINC_1_n, RINC_2_n, RINC_3_n;
  wire [1:0] BSRC, CS, PCSEL;
  wire [2:0] BS, COS, DCL, DCLd, DOSEL, PAAR, PADR, RS;
  wire [3:0] B, O2H, O2L, OPA, OPR, PCH, PCL, PCM, RES, REVEN, RINC, RODD, RSEL, WD;

  Multiplexer #(.select(1), .enable("false"), .width(4)) multiplexer_1 (
    .in0(AKKU), .in1(RINC), .out(WD), .sel(RF_DSEL));
  not not_1 (RINC_3_n, RINC[3]);
  not not_2 (DCL_0_n, DCL[0]);
  Register #(.width(4)) IR_hoch (.D(D_EIN), .en(IRH_WE), .Q(OPR), .clk(CLK));  // open: clr
  Register #(.width(4)) u_Akku (.D(RES), .en(ACC_WE), .Q(AKKU), .clk(CLK));  // open: clr
  Steuerwerk steuerwerk_1 (
    .PH(PHASE), .C2(C2), .OPR(OPR), .OPA(OPA), .IRH_WE(IRH_WE), .IRL_WE(IRL_WE), .O2H_WE(O2H_WE),
    .O2L_WE(O2L_WE), .PC_WE(PC_WE), .PC_WEC(PC_WEC), .PUSH(PUSH), .POP(POP), .ACC_WE(ACC_WE), .CY_WE(CY_WE),
    .RF_WES(RF_WES), .RF_WEP(RF_WEP), .RF_DSEL(RF_DSEL), .PAIR0(PAIR0), .CMROM(CMROM), .CMRAM(CMRAM),
    .C2_WE(C2_WE), .C2_D(C2_D), .DCL_WE(DCL_WE), .CONDSEL(CONDSEL), .PCSEL(PCSEL), .BS(BS), .CS(CS), .RS(RS),
    .COS(COS), .BSRC(BSRC), .DOSEL(DOSEL));
  xor xor_1 (JCN_OK, JC, OPA[3]);
  Adressstapel adressstapel_1 (
    .CLK(CLK), .PUSH(PUSH), .POP(POP), .WE(PCWE), .PCSEL(PCSEL), .O2H(O2H), .O2L(O2L), .OPA(OPA),
    .REVEN(REVEN), .RODD(RODD), .PCL(PCL), .PCM(PCM), .PCH(PCH), .SP(SP));
  and and_1 (CM_RAM2, CMRAM, DCL[1]);
  Buendel_12 buendel_12_1 (
    .b0(PCL[0]), .b1(PCL[1]), .b2(PCL[2]), .b3(PCL[3]), .b4(PCM[0]), .b5(PCM[1]), .b6(PCM[2]), .b7(PCM[3]),
    .b8(PCH[0]), .b9(PCH[1]), .b10(PCH[2]), .b11(PCH[3]), .bus(PC));
  and and_2 (AKKU0, ACC_0_n, ACC_1_n, ACC_2_n, ACC_3_n);
  not not_3 (ACC_0_n, AKKU[0]);
  not not_4 (DCL_1_n, DCL[1]);
  Indexregister indexregister_1 (
    .CLK(CLK), .PADR(PADR), .UNGERADE(OPA[0]), .WD(WD), .DH(O2H), .DL(O2L), .WE1(RF_WES), .WE2(RF_WEP),
    .REVEN(REVEN), .RODD(RODD), .RSEL(RSEL), .P0(R0R1), .P1(R2R3), .P2(R4R5), .P3(R6R7), .P4(R8R9),
    .P5(R10R11), .P6(R12R13), .P7(R14R15));
  and and_3 (CM_RAM3, CMRAM, DCL[2]);
  Register #(.width(4)) IR_tief (.D(D_EIN), .en(IRL_WE), .Q(OPA), .clk(CLK));  // open: clr
  Register #(.width(1)) u_Carry (.D(COUT), .en(CY_WE), .Q(CARRY), .clk(CLK));  // open: clr
  and and_4 (g6, OPA[2], AKKU0);
  and and_5 (g9, RINC_0_n, RINC_1_n, RINC_2_n, RINC_3_n);
  not not_5 (ACC_1_n, AKKU[1]);
  Buendel_3 buendel_3_1 (.b0(AKKU[0]), .b1(AKKU[1]), .b2(AKKU[2]), .bus(DCLd));
  not not_6 (DCL_2_n, DCL[2]);
  Adder #(.width(4)) adder_1 (.a(RSEL), .b(4'b0000), .out(RINC), .cin(1'b1));  // open: cout
  and and_6 (g7, OPA[1], CARRY);
  not not_7 (RINC_0_n, RINC[0]);
  not not_8 (ISZ_OK, g9);
  Register #(.width(4)) Operand_hoch (.D(D_EIN), .en(O2H_WE), .Q(O2H), .clk(CLK));  // open: clr
  Register #(.width(3)) u_DCL (.D(DCLd), .en(DCL_WE), .Q(DCL), .clk(CLK));  // open: clr
  Buendel_8 buendel_8_1 (
    .b0(OPA[0]), .b1(OPA[1]), .b2(OPA[2]), .b3(OPA[3]), .b4(OPR[0]), .b5(OPR[1]), .b6(OPR[2]), .b7(OPR[3]),
    .bus(IR));
  Buendel_3 buendel_3_2 (.b0(OPA[1]), .b1(OPA[2]), .b2(OPA[3]), .bus(PAAR));
  not not_9 (ACC_2_n, AKKU[2]);
  and and_7 (g11, DCL_0_n, DCL_1_n, DCL_2_n);
  Taktgeber taktgeber_1 (.CLK(CLK), .PH(PHASE), .SYNC(SYNC));
  not not_10 (nTEST, TEST);
  not not_11 (RINC_1_n, RINC[1]);
  Multiplexer #(.select(1), .enable("false")) multiplexer_2 (.in0(JCN_OK), .in1(ISZ_OK), .out(BED), .sel(CONDSEL));
  Multiplexer #(.select(2), .enable("false"), .width(4)) multiplexer_3 (
    .in0(RSEL), .in1(D_EIN), .in2(OPA), .in3(4'b0000), .out(B), .sel(BSRC));
  Register #(.width(4)) Operand_tief (.D(D_EIN), .en(O2L_WE), .Q(O2L), .clk(CLK));  // open: clr
  not not_12 (ACC_3_n, AKKU[3]);
  Multiplexer #(.select(3), .enable("false"), .width(4)) multiplexer_4 (
    .in0(4'b0000), .in1(PCL), .in2(PCM), .in3(PCH), .in4(AKKU), .in5(REVEN), .in6(RODD), .in7(4'b0000),
    .out(D_AUS), .sel(DOSEL));
  and and_8 (CM_RAM0, CMRAM, g11);
  Multiplexer #(.select(1), .enable("false"), .width(3)) multiplexer_5 (
    .in0(PAAR), .in1(3'b000), .out(PADR), .sel(PAIR0));
  and and_9 (g8, OPA[0], nTEST);
  not not_13 (RINC_2_n, RINC[2]);
  and and_10 (g10, PC_WEC, BED);
  ALU alu_1 (.A(AKKU), .CY(CARRY), .B(B), .BS(BS), .CS(CS), .RS(RS), .COS(COS), .RES(RES), .COUT(COUT));
  Register #(.width(1)) Zyklus2 (.D(C2_D), .en(C2_WE), .Q(C2), .clk(CLK));  // open: clr
  or or_1 (JC, g6, g7, g8);
  or or_2 (PCWE, PC_WE, g10);
  and and_11 (CM_ROM, CMROM, CMROM);
  and and_12 (CM_RAM1, CMRAM, DCL[0]);

  // Other names for the same wires on the sheet: ACC[3:0] = AKKU; ACC_0 = AKKU[0]; ACC_1 = AKKU[1]; ACC_2 = AKKU[2];
  //   ACC_3 = AKKU[3]; CY = CARRY; DCL_0 = DCL[0]; DCL_1 = DCL[1]; DCL_2 = DCL[2]; IR8[7:0] = IR; OPA_0 = OPA[0];
  //   OPA_1 = OPA[1]; OPA_2 = OPA[2]; OPA_3 = OPA[3]; OPR_0 = OPR[0]; OPR_1 = OPR[1]; OPR_2 = OPR[2]; OPR_3 = OPR[3];
  //   P0[7:0] = R0R1; P1[7:0] = R2R3; P2[7:0] = R4R5; P3[7:0] = R6R7; P4[7:0] = R8R9; P5[7:0] = R10R11;
  //   P6[7:0] = R12R13; P7[7:0] = R14R15; PC12[11:0] = PC; PCH_0 = PCH[0]; PCH_1 = PCH[1]; PCH_2 = PCH[2];
  //   PCH_3 = PCH[3]; PCL_0 = PCL[0]; PCL_1 = PCL[1]; PCL_2 = PCL[2]; PCL_3 = PCL[3]; PCM_0 = PCM[0]; PCM_1 = PCM[1];
  //   PCM_2 = PCM[2]; PCM_3 = PCM[3]; PH[2:0] = PHASE; RINC_0 = RINC[0]; RINC_1 = RINC[1]; RINC_2 = RINC[2];
  //   RINC_3 = RINC[3]

  // Notes on the sheet:
  //   Intel 4004 auf Registertransferebene. Datenbus aufgeteilt: D_EIN (wired-OR aller Bausteine) und D_AUS.
  //   Kein Tristate noetig: jeder Baustein legt 0 an, wenn er nicht treibt; im System werden alle per ODER zusammengefasst.
endmodule

module Peripherie_Phase (
  input  CLK,
  input  SYNC,
  output T0,
  output T1,
  output T2,
  output T3,
  output T4,
  output T5,
  output T6,
  output T7
);

  wire [2:0] Q, QN, s12;

  Register #(.width(3)) Phase (.D(QN), .Q(Q), .clk(CLK));  // open: en, clr
  Adder #(.width(3)) adder_1 (.a(Q), .b(3'b001), .out(s12));  // open: cin, cout
  Multiplexer #(.select(1), .enable("false"), .width(3)) multiplexer_1 (.in0(s12), .in1(3'b000), .out(QN), .sel(SYNC));
  Dekoder_3zu8 dekoder_3zu8_1 (
    .A(Q), .EN(1'b1), .Y0(T0), .Y1(T1), .Y2(T2), .Y3(T3), .Y4(T4), .Y5(T5), .Y6(T6), .Y7(T7));

  // Notes on the sheet:
  //   Eigener Phasenzaehler der Peripheriebausteine, mit SYNC (X3) auf A1 gesetzt - wie in 4001/4002.
endmodule

module ROM_4001 (
  input  CLK,
  input  SYNC,
  input  CM_ROM,
  input  [3:0] BUS,
  input  [7:0] ROMDATEN,
  input  [3:0] PORT_EIN,
  output [11:0] ADRESSE,
  output [3:0] PORT_AUS,
  output [3:0] D_AUS
);

  wire BUS_0_n, BUS_1_n, BUS_2_n, BUS_3_n, CHIP0, g13, g14, g15, IOOP_0_n, IOOP_2_n, IOOP_3_n, RDR, SEL, T0,
       T1, T2, T3, T4, T5, T6, T7, WRR;
  wire [3:0] AH, AL, AM, DM1, DM2, IOd, IOOP, OPA, OPR;

  Multiplexer #(.select(1), .enable("false"), .width(4)) multiplexer_1 (
    .in0(4'b1111), .in1(BUS), .out(IOd), .sel(CM_ROM));
  not not_1 (IOOP_3_n, IOOP[3]);
  Multiplexer #(.select(1), .enable("false"), .width(4)) multiplexer_2 (.in0(4'b0000), .in1(OPR), .out(DM1), .sel(T3));
  Register #(.width(4)) Adr_A1 (.D(BUS), .en(T0), .Q(AL), .clk(CLK));  // open: clr
  Register #(.width(4)) Ausgabeport (.D(BUS), .en(WRR), .Q(PORT_AUS), .clk(CLK));  // open: clr
  Buendel_12 buendel_12_1 (
    .b0(AL[0]), .b1(AL[1]), .b2(AL[2]), .b3(AL[3]), .b4(AM[0]), .b5(AM[1]), .b6(AM[2]), .b7(AM[3]),
    .b8(AH[0]), .b9(AH[1]), .b10(AH[2]), .b11(AH[3]), .bus(ADRESSE));
  and and_1 (CHIP0, BUS_0_n, BUS_1_n, BUS_2_n, BUS_3_n);
  Multiplexer #(.select(1), .enable("false"), .width(4)) multiplexer_3 (.in0(DM1), .in1(OPA), .out(DM2), .sel(T4));
  Register #(.width(4)) Adr_A2 (.D(BUS), .en(T1), .Q(AM), .clk(CLK));  // open: clr
  Peripherie_Phase peripherie_phase_1 (
    .CLK(CLK), .SYNC(SYNC), .T0(T0), .T1(T1), .T2(T2), .T3(T3), .T4(T4), .T5(T5), .T6(T6), .T7(T7));
  and and_2 (g13, T6, CM_ROM);
  and and_3 (g14, IOOP_0_n, IOOP[1], IOOP_2_n, IOOP_3_n);
  Multiplexer #(.select(1), .enable("false"), .width(4)) multiplexer_4 (
    .in0(DM2), .in1(PORT_EIN), .out(D_AUS), .sel(RDR));
  not not_2 (BUS_0_n, BUS[0]);
  Register #(.width(4)) Adr_A3 (.D(BUS), .en(T2), .Q(AH), .clk(CLK));  // open: clr
  and and_4 (WRR, T6, SEL, g14);
  Buendel_4 buendel_4_1 (.b0(ROMDATEN[4]), .b1(ROMDATEN[5]), .b2(ROMDATEN[6]), .b3(ROMDATEN[7]), .bus(OPR));
  not not_3 (BUS_1_n, BUS[1]);
  Register #(.width(4)) IO_Befehl (.D(IOd), .en(T4), .Q(IOOP), .clk(CLK));  // open: clr
  not not_4 (BUS_2_n, BUS[2]);
  not not_5 (IOOP_0_n, IOOP[0]);
  and and_5 (g15, IOOP_0_n, IOOP[1], IOOP_2_n, IOOP[3]);
  Register #(.width(1)) Chip0_gewaehlt (.D(CHIP0), .en(g13), .Q(SEL), .clk(CLK));  // open: clr
  Buendel_4 buendel_4_2 (.b0(ROMDATEN[0]), .b1(ROMDATEN[1]), .b2(ROMDATEN[2]), .b3(ROMDATEN[3]), .bus(OPA));
  not not_6 (BUS_3_n, BUS[3]);
  not not_7 (IOOP_2_n, IOOP[2]);
  and and_6 (RDR, T6, SEL, g15);

  // Other names for the same wires on the sheet: ADR[11:0] = ADRESSE; AH_0 = AH[0]; AH_1 = AH[1]; AH_2 = AH[2];
  //   AH_3 = AH[3]; AL_0 = AL[0]; AL_1 = AL[1]; AL_2 = AL[2]; AL_3 = AL[3]; AM_0 = AM[0]; AM_1 = AM[1]; AM_2 = AM[2];
  //   AM_3 = AM[3]; BUS_0 = BUS[0]; BUS_1 = BUS[1]; BUS_2 = BUS[2]; BUS_3 = BUS[3]; IOOP_0 = IOOP[0];
  //   IOOP_1 = IOOP[1]; IOOP_2 = IOOP[2]; IOOP_3 = IOOP[3]; PORT[3:0] = PORT_AUS; ROMDATEN_0 = ROMDATEN[0];
  //   ROMDATEN_1 = ROMDATEN[1]; ROMDATEN_2 = ROMDATEN[2]; ROMDATEN_3 = ROMDATEN[3]; ROMDATEN_4 = ROMDATEN[4];
  //   ROMDATEN_5 = ROMDATEN[5]; ROMDATEN_6 = ROMDATEN[6]; ROMDATEN_7 = ROMDATEN[7]

  // Notes on the sheet:
  //   ROM-Bank (bis 16 x 4001 in einem Speicher): Adresse wird in A1..A3 nibbleweise vom Bus uebernommen,
  //   in M1/M2 wird OPR/OPA ausgegeben. I/O-Port nur fuer Chip 0: SRC mit oberem Nibble 0 waehlt ihn, WRR/RDR.
endmodule

module RAM_4002 (
  input  CLK,
  input  SYNC,
  input  CM_RAM,
  input  [3:0] BUS,
  output [3:0] PORT_AUS,
  output [3:0] D_AUS
);

  wire AKTIV, BUS_2_n, BUS_3_n, CHIP0, g16, g17, g18, g19, g20, IOOP_0_n, IOOP_1_n, IOOP_2_n, IOOP_3_n, IOV,
       ISTSTATUS, LESEN, n21, SEL, SRC_X2, SRCF, T0, T1, T2, T3, T4, T5, T6, T7, WMP, WRM, WRn;
  wire [1:0] REG, REGd;
  wire [3:0] HAUPT, IOOP, LESEWERT, SADR, STATUS, ZEICHEN;
  wire [5:0] MADR;

  not not_1 (BUS_3_n, BUS[3]);
  and and_1 (AKTIV, T6, IOV, SEL);
  not not_2 (IOOP_2_n, IOOP[2]);
  Register #(.width(1)) Chip0_gewaehlt (.D(CHIP0), .en(SRC_X2), .Q(SEL), .clk(CLK));  // open: clr
  Register #(.width(4)) IO_Befehl (.D(BUS), .en(g17), .Q(IOOP), .clk(CLK));  // open: clr
  and and_2 (WMP, AKTIV, g19);
  RAM #(.addrWidth(4), .dataWidth(4), .bus("separate")) Status_4x4 (
    .addr(SADR), .din(BUS), .data(STATUS), .str(WRn), .clk(CLK));  // open: sel, ld, clr
  not not_3 (BUS_2_n, BUS[2]);
  not not_4 (IOOP_3_n, IOOP[3]);
  Register #(.width(4)) Ausgabeport (.D(BUS), .en(WMP), .Q(PORT_AUS), .clk(CLK));  // open: clr
  and and_3 (WRn, AKTIV, IOOP_3_n, IOOP[2]);
  Register #(.width(2)) Register (.D(REGd), .en(SRC_X2), .Q(REG), .clk(CLK));  // open: clr
  and and_4 (ISTSTATUS, IOOP[3], IOOP[2]);
  and and_5 (CHIP0, BUS_3_n, BUS_2_n);
  Buendel_6 buendel_6_1 (
    .b0(ZEICHEN[0]), .b1(ZEICHEN[1]), .b2(ZEICHEN[2]), .b3(ZEICHEN[3]), .b4(REG[0]), .b5(REG[1]), .bus(MADR));
  Register #(.width(1)) SRC_aktiv (.D(CM_RAM), .en(T6), .Q(SRCF), .clk(CLK));  // open: clr
  Peripherie_Phase peripherie_phase_1 (
    .CLK(CLK), .SYNC(SYNC), .T0(T0), .T1(T1), .T2(T2), .T3(T3), .T4(T4), .T5(T5), .T6(T6), .T7(T7));
  and and_6 (g18, IOOP_0_n, IOOP_1_n, IOOP_2_n, IOOP_3_n);
  and and_7 (g20, IOOP_0_n, IOOP[1], IOOP_2_n, IOOP[3]);
  Multiplexer #(.select(1), .enable("false"), .width(4)) multiplexer_1 (
    .in0(HAUPT), .in1(STATUS), .out(LESEWERT), .sel(ISTSTATUS));
  RAM #(.addrWidth(6), .dataWidth(4), .bus("separate")) Hauptzeichen_4x16 (
    .addr(MADR), .din(BUS), .data(HAUPT), .str(WRM), .clk(CLK));  // open: sel, ld, clr
  Buendel_2 buendel_2_1 (.b0(BUS[0]), .b1(BUS[1]), .bus(REGd));
  not not_5 (IOOP_0_n, IOOP[0]);
  not not_6 (n21, g20);
  Register #(.width(4)) u_Zeichen (.D(BUS), .en(g16), .Q(ZEICHEN), .clk(CLK));  // open: clr
  and and_8 (WRM, AKTIV, g18);
  Multiplexer #(.select(1), .enable("false"), .width(4)) multiplexer_2 (
    .in0(4'b0000), .in1(LESEWERT), .out(D_AUS), .sel(LESEN));
  and and_9 (g16, T7, SRCF);
  not not_7 (IOOP_1_n, IOOP[1]);
  and and_10 (LESEN, AKTIV, IOOP[3], n21);
  Buendel_4 buendel_4_1 (.b0(IOOP[0]), .b1(IOOP[1]), .b2(REG[0]), .b3(REG[1]), .bus(SADR));
  Register #(.width(1)) IO_aktiv (.D(CM_RAM), .en(T4), .Q(IOV), .clk(CLK));  // open: clr
  and and_11 (SRC_X2, T6, CM_RAM);
  and and_12 (g19, IOOP[0], IOOP_1_n, IOOP_2_n, IOOP_3_n);
  and and_13 (g17, T4, CM_RAM);

  // Other names for the same wires on the sheet: BUS_0 = BUS[0]; BUS_1 = BUS[1]; BUS_2 = BUS[2]; BUS_3 = BUS[3];
  //   IOOP_0 = IOOP[0]; IOOP_1 = IOOP[1]; IOOP_2 = IOOP[2]; IOOP_3 = IOOP[3]; PORT[3:0] = PORT_AUS; REG_0 = REG[0];
  //   REG_1 = REG[1]; ZEICHEN_0 = ZEICHEN[0]; ZEICHEN_1 = ZEICHEN[1]; ZEICHEN_2 = ZEICHEN[2]; ZEICHEN_3 = ZEICHEN[3]

  // Notes on the sheet:
  //   Ein 4002 (Bank 0, Chip 0): 4 Register x 16 Hauptzeichen + 4 Statuszeichen, 4-Bit-Ausgabeport.
  //   SRC in X2/X3 waehlt Chip, Register und Zeichen; I/O-Befehle werden in M2 mitgelesen und in X2 ausgefuehrt.
endmodule

module System_4004 (
  input  TEST,
  input  [3:0] PORT_EIN,
  output [3:0] AKKU,
  output CARRY,
  output [11:0] PC,
  output [7:0] IR,
  output [2:0] PHASE,
  output [1:0] SP,
  output SYNC,
  output [3:0] BUS,
  output [7:0] R0R1,
  output [7:0] R2R3,
  output [7:0] R4R5,
  output [7:0] R6R7,
  output [7:0] R8R9,
  output [7:0] R10R11,
  output [7:0] R12R13,
  output [7:0] R14R15,
  output [3:0] ROM_PORT,
  output [3:0] RAM_PORT
);

  wire CLK, CM_RAM0, CM_RAM1, CM_RAM2, CM_RAM3, CM_ROM;
  wire [3:0] CPU_D, RAM_D, ROM_D;
  wire [7:0] ROMDATEN;
  wire [11:0] ROMADR;

  Clock clock_1 (.out(CLK));
  RAM_4002 ram_4002_1 (.CLK(CLK), .SYNC(SYNC), .CM_RAM(CM_RAM0), .BUS(BUS), .PORT_AUS(RAM_PORT), .D_AUS(RAM_D));
  CPU_4004 cpu_4004_1 (
    .CLK(CLK), .D_EIN(BUS), .TEST(TEST), .D_AUS(CPU_D), .SYNC(SYNC), .CM_ROM(CM_ROM), .CM_RAM0(CM_RAM0),
    .CM_RAM1(CM_RAM1), .CM_RAM2(CM_RAM2), .CM_RAM3(CM_RAM3), .AKKU(AKKU), .CARRY(CARRY), .PC(PC), .IR(IR),
    .PHASE(PHASE), .SP(SP), .R0R1(R0R1), .R2R3(R2R3), .R4R5(R4R5), .R6R7(R6R7), .R8R9(R8R9), .R10R11(R10R11),
    .R12R13(R12R13), .R14R15(R14R15));
  assign BUS = CPU_D | ROM_D | RAM_D;  // OR_Gate or_1, 4 bits wide
  ROM #(.addrWidth(12), .dataWidth(8)) Programm (.addr(ROMADR), .data(ROMDATEN));  // open: sel
  ROM_4001 rom_4001_1 (
    .CLK(CLK), .SYNC(SYNC), .CM_ROM(CM_ROM), .BUS(BUS), .ROMDATEN(ROMDATEN), .PORT_EIN(PORT_EIN),
    .ADRESSE(ROMADR), .PORT_AUS(ROM_PORT), .D_AUS(ROM_D));

  // Notes on the sheet:
  //   Intel-4004-System: CPU, ROM-Bank (4001) mit Programm-ROM, ein RAM-Chip 4002. Datenbus als wired-OR.
  //   Programm: ROM "Programm" anklicken (Web-Simulator) bzw. Inhalt bearbeiten (Logisim). Ein Befehl = 8 Subzyklen = 16 Taktschritte.
  //   TEST-Pin fuer JCN, PORT_EIN wird mit RDR gelesen (nach SRC auf ROM-Chip 0).
  //   contents of Programm (hex, n*v repeats v):
  //   20 0 21 d0 b2 d1 b3 f1 a2 83 b3 b2 a3 e2 e1 40 7
endmodule
