# Fritzing sketch Z3-1BitRam (saved by Fritzing 1.0.1rc)

parts:
  D1 = Diode [package=diode-1n4148]  # not connected
  S4 = Momentary Switch [package=ksa_sealed_tac_switch]
  LED3 = smd LED [color="Orange (620nm)" package="0603 [SMD]"]  # not connected
  R3 = Resistor [tolerance=±5% resistance=220 package="2512 [SMD]"]
  8-Channel_Relay1 = 8-Channel 5v Relay Shield [package=relay-8ch5v10a]
  S5 = Momentary Switch [package=ksa_sealed_tac_switch]
  OMRON5 = OMRON PCB Power Relay – G5LE [part_number="G5LE-1\n" package=THT]  # not connected

nets:
  N1: S4.3, 8-Channel_Relay1.IN1, 8-Channel_Relay1.K1-Off, S5.4
  N2: R3.Pin_1, 8-Channel_Relay1.K1-On

custom parts:
  8-Channel 5v Relay Shield: 8 Channel 5v Relay Shield w. 2x SPD-06VDC-SD-C
