# Fritzing sketch Z3-Gate-Halfadder (saved by Fritzing 1.0.1rc)
breadboards: 1

parts:
  D1 = Diode [package=diode-1n4148]
  R1 = Resistor [tolerance=±5% resistance=220 package="2512 [SMD]"]
  LED1 = smd LED [color="Orange (620nm)" package="0603 [SMD]"]
  LED2 = smd LED [color="Yellow (592nm)" package="0603 [SMD]"]
  S1 = Momentary Switch [package=ksa_sealed_tac_switch]
  S2 = Momentary Switch [package=ksa_sealed_tac_switch]
  OMRON1 = OMRON PCB Power Relay – G5LE [part_number="G5LE-1\n" package=THT]
  OMRON2 = OMRON PCB Power Relay – G5LE [part_number="G5LE-1\n" package=THT]
  D3 = Diode [package=diode-1n4148]
  OMRON3 = OMRON PCB Power Relay – G5LE [part_number="G5LE-1\n" package=THT]
  OMRON4 = OMRON PCB Power Relay – G5LE [part_number="G5LE-1\n" package=THT]
  D4 = Diode [package=diode-1n4148]
  D5 = Diode [package=diode-1n4148]
  R2 = Resistor [tolerance=±5% resistance=220 package="2512 [SMD]"]
  8-Channel_Relay1 = 8-Channel 5v Relay Shield [package=relay-8ch5v10a]  # not connected

nets:
  N1: D1.C, S2.2, OMRON1.COIL1, OMRON2.COIL1, D3.C
  N2: R1.Pin_0, LED1.anode
  N3: R1.Pin_1, OMRON1.COIL2, OMRON2.COIL2, OMRON4.COIL2, R2.Pin_1
  N4: LED1.cathode, OMRON3.A, OMRON4.B
  N5: LED2.cathode, OMRON2.B, OMRON3.B
  N6: LED2.anode, R2.Pin_0
  N7: S1.1, S2.1, OMRON1.C, OMRON2.C
  N8: S1.2, OMRON3.COIL1, OMRON4.COIL1, D4.C, D5.C
  N9: OMRON1.A, OMRON4.C
  N10: OMRON1.B, OMRON3.C

custom parts:
  8-Channel 5v Relay Shield: 8 Channel 5v Relay Shield w. 2x SPD-06VDC-SD-C
